// Logisim project sim.circ as structural Verilog: 3 circuits, main circuit main
module main (
  input  in_1,
  input  in_2,
  input  in_3,
  input  in_4,
  input  in_5,
  input  in_6,
  input  in_7,
  input  in_8,
  input  in_9,
  input  in_10,
  input  in_11,
  input  in_12,
  input  in_13,
  input  in_14,
  input  in_15,
  input  in_16,
  input  in_17,
  input  in_18,
  input  in_19,
  input  in_20,
  input  in_21,
  input  in_22,
  input  in_23,
  input  in_24
);

  wire CLK, not_1_out, not_2_out, not_3_out, undriven;
  wire [3:0] STEPPER_q;
  wire [15:0] A_q, alu_1_s, B_q, C_q, controlled_buffer_1_out, controlled_buffer_2_out, D_q, E_q, IR_q,
       MAR_q, MDR_q, PC_q, ram_1_data;

  not not_1 (not_1_out, CLK);
  Counter #(.max('hf), .width(4)) STEPPER (
    .load(1'b0), .count(1'b1), .Q(STEPPER_q), .up(1'b1), .clk(not_1_out), .clr(1'b0));  // open: D, carry
  Clock clock_1 (.out(CLK));
  RAM #(.addrWidth(16), .asyncread("true"), .dataWidth(16), .databus("bidir"), .\type ("nonvolatile")) ram_1 (
    .addr(controlled_buffer_1_out), .we(in_13), .oe(in_19), .clk(CLK), .data(ram_1_data));
  not not_2 (not_2_out, CLK);
  not not_3 (not_3_out, in_3);
  assign controlled_buffer_1_out = not_3_out ? PC_q : 16'bz;  // Controlled_Buffer controlled_buffer_1
  Multiplexer multiplexer_1 (.in0(not_2_out), .in1(CLK), .sel(in_15));  // open: out
  CTRL ctrl_1 (
    .STEP(STEPPER_q), .I(IR_q));  // open: MDR_OE, PC_OE, IR_OE, MDR_WE, MAR_WE, PC_WE, PC_INC, A_WE, B_WE, C_WE, D_WE, E_WE, A_OE, B_OE, C_OE, D_OE, E_OE
  Register #(.width(16)) IR (.D(ram_1_data), .en(in_20), .clk(CLK), .Q(IR_q));  // open: clr
  assign controlled_buffer_2_out = in_14 ? PC_q : 16'bz;  // Controlled_Buffer controlled_buffer_2
  Counter #(.max('hffff), .width(16)) PC (
    .load(in_15), .D(controlled_buffer_2_out), .count(in_1), .Q(PC_q), .up(1'b1), .clk(undriven), .clr(1'b0));  // open: carry
  Register #(.width(16)) MAR (.D(controlled_buffer_2_out), .en(in_9), .clk(CLK), .Q(MAR_q));  // open: clr
  Register #(.width(16)) MDR (.D(ram_1_data), .en(in_4), .clk(CLK), .Q(MDR_q));  // open: clr
  assign controlled_buffer_1_out = in_3 ? MAR_q : 16'bz;  // Controlled_Buffer controlled_buffer_3
  assign ram_1_data = in_2 ? controlled_buffer_2_out : 16'bz;  // Controlled_Buffer controlled_buffer_4
  assign controlled_buffer_2_out = in_8 ? MDR_q : 16'bz;  // Controlled_Buffer controlled_buffer_5
  Register #(.width(16)) A (.D(controlled_buffer_2_out), .en(in_6), .clk(CLK), .Q(A_q));  // open: clr
  Register #(.width(16)) B (.D(controlled_buffer_2_out), .en(in_11), .clk(CLK), .Q(B_q));  // open: clr
  Register #(.width(16)) C (.D(controlled_buffer_2_out), .en(in_17), .clk(CLK), .Q(C_q));  // open: clr
  Register #(.width(16)) D (.D(controlled_buffer_2_out), .en(in_22), .clk(CLK), .Q(D_q));  // open: clr
  Register #(.width(16)) E (.D(controlled_buffer_2_out), .en(in_24), .clk(CLK), .Q(E_q));  // open: clr
  assign controlled_buffer_2_out = in_5 ? A_q : 16'bz;  // Controlled_Buffer controlled_buffer_6
  assign controlled_buffer_2_out = in_10 ? B_q : 16'bz;  // Controlled_Buffer controlled_buffer_7
  assign controlled_buffer_2_out = in_16 ? C_q : 16'bz;  // Controlled_Buffer controlled_buffer_8
  assign controlled_buffer_2_out = in_21 ? D_q : 16'bz;  // Controlled_Buffer controlled_buffer_9
  assign controlled_buffer_2_out = in_23 ? E_q : 16'bz;  // Controlled_Buffer controlled_buffer_10
  assign controlled_buffer_2_out = in_18 ? alu_1_s : 16'bz;  // Controlled_Buffer controlled_buffer_11
  ALU alu_1 (
    .A(controlled_buffer_2_out), .A_WE(in_7), .B(controlled_buffer_2_out), .B_WE(in_12), .CLK(CLK),
    .OP(IR_q[3:0]), .S(alu_1_s));  // open: C, Z, P

  // Other names for the same wires on the sheet: A_OE = in_5; A_WE = in_6; ALU_A_WE = in_7; ALU_B_WE = in_12;
  //   ALU_OE = in_18; B_OE = in_10; B_WE = in_11; C_OE = in_16; C_WE = in_17; D_OE = in_21; D_WE = in_22;
  //   E_OE = in_23; E_WE = in_24; IR_WE = in_20; MAR2RAM = in_3; MAR_WE = in_9; MDR_DB = in_2; MDR_OE = in_8;
  //   MDR_WE = in_4; PC_INC = in_1; PC_OE = in_14; PC_WE = in_15; RAM_OE = in_19; RAM_WE = in_13
endmodule

module ALU (
  input  [15:0] A,
  input  A_WE,
  input  [15:0] B,
  input  B_WE,
  input  CLK,
  input  [3:0] OP,
  output [15:0] S,
  output C,
  output Z,
  output P
);

  wire and_2_out, not_1_out, not_2_out, not_3_out, or_2_out, xor_3_out, xor_4_out;
  wire [15:0] adder_1_out, and_1_out, bit_extender_1_out, multiplexer_1_out, multiplexer_2_out,
       multiplexer_3_out, multiplexer_4_out, or_1_out, register_1_q, register_2_q, shifter_1_out,
       shifter_2_out, xor_1_out, xor_2_out;

  Register #(.width(16)) register_1 (.D(A), .en(A_WE), .clk(CLK), .Q(register_1_q));  // open: clr
  Register #(.width(16)) register_2 (.D(B), .en(B_WE), .clk(CLK), .Q(register_2_q));  // open: clr
  not not_1 (not_1_out, OP[0]);
  assign bit_extender_1_out = {{15{not_1_out}}, not_1_out};  // Bit_Extender bit_extender_1
  assign xor_1_out = register_2_q ^ bit_extender_1_out;  // XOR_Gate xor_1, 16 bits wide
  assign or_1_out = register_1_q | register_2_q;  // OR_Gate or_1, 16 bits wide
  Multiplexer #(.width(16)) multiplexer_1 (.in0(or_1_out), .in1(and_1_out), .out(multiplexer_1_out), .sel(not_2_out));
  assign and_1_out = register_1_q & register_2_q;  // AND_Gate and_1, 16 bits wide
  not not_2 (not_2_out, OP[0]);
  assign xor_2_out = register_1_q ^ register_2_q;  // XOR_Gate xor_2, 16 bits wide
  Multiplexer #(.width(16)) multiplexer_2 (
    .in0(xor_2_out), .in1(shifter_1_out), .out(multiplexer_2_out), .sel(not_3_out));
  Shifter #(.width(16)) shifter_1 (.in(register_1_q), .\dist (register_2_q[3:0]), .out(shifter_1_out));
  not not_3 (not_3_out, OP[0]);
  Shifter #(.shift("lr"), .width(16)) shifter_2 (.in(register_1_q), .\dist (register_2_q[3:0]), .out(shifter_2_out));
  Adder #(.width(16)) adder_1 (.a(register_1_q), .b(xor_1_out), .out(adder_1_out), .cin(not_1_out), .cout(C));
  xor xor_3 (xor_3_out, OP[0], OP[1]);
  xor xor_4 (xor_4_out, OP[0], OP[1]);
  Multiplexer #(.width(16)) multiplexer_3 (
    .in0(adder_1_out), .in1(multiplexer_1_out), .out(multiplexer_3_out), .sel(xor_3_out));
  Multiplexer #(.width(16)) multiplexer_4 (
    .in0(multiplexer_2_out), .in1(shifter_2_out), .out(multiplexer_4_out), .sel(xor_4_out));
  Multiplexer #(.width(16)) multiplexer_5 (.in0(multiplexer_3_out), .in1(multiplexer_4_out), .out(S), .sel(or_2_out));
  or or_2 (or_2_out, and_2_out, OP[3]);
  and and_2 (and_2_out, OP[0], OP[1], OP[2]);

  // Notes on the sheet:
  //   0011: A+B
  //   0100: A-B
  //   0101: A v B
  //   0110: A ^ B
  //   0111: A xor B
  //   1000: A << B
  //   1001: A >> B
endmodule

module CTRL (
  input  [3:0] STEP,
  input  [15:0] I,
  output MDR_OE,
  output PC_OE,
  output IR_OE,
  output MDR_WE,
  output MAR_WE,
  output PC_WE,
  output PC_INC,
  output A_WE,
  output B_WE,
  output C_WE,
  output D_WE,
  output E_WE,
  output A_OE,
  output B_OE,
  output C_OE,
  output D_OE,
  output E_OE
);

  wire [23:0] rom_1_data;

  ROM #(.dataWidth(24)) rom_1 (.addr({I[3:0], STEP}), .data(rom_1_data));
  ROM #(.dataWidth(24)) rom_2 ();  // open: addr, data
endmodule
